# Fritzing sketch skematik rangkaian (saved by Fritzing 0.8.7b)
breadboards: 1

parts:
  LED1 = LED - 5mm [color="Red (633nm)" package="5 mm [THT]"]
  R1 = Resistor [tolerance=±5% resistance=220 package=THT]
  Raspberry_Pi_1 = Raspberry Pi 3
  Part1 = SRF05 Ultrasonic Rangefinder
  DHT1 = DHT11 Humitidy and Temperature Sensor
  R2 = Resistor [tolerance=±5% resistance=220 package=THT]
  R3 = Resistor [tolerance=±5% resistance=220 package=THT]
  R4 = Resistor [tolerance=±5% resistance=220 package=THT]

nets:
  N1: LED1.cathode, Raspberry_Pi_1.GIPO21
  N2: LED1.anode, R1.Pin_0
  GND: R1.Pin_1, Raspberry_Pi_1.GND, Part1.GND, DHT1.GND, R3.Pin_0
  3V3: Raspberry_Pi_1.3v3, DHT1.VDD, R4.Pin_0
  N3: Raspberry_Pi_1.GIPO4, Raspberry_Pi_1.GIPO14, DHT1.DATA, R4.Pin_1
  N4: Raspberry_Pi_1.GIPO24, R2.Pin_1, R3.Pin_1
  N5: Raspberry_Pi_1.GIPO23, Part1.Trig
  5V: Raspberry_Pi_1.5V, Part1.VCC
  N6: Part1.Echo, R2.Pin_0

custom parts:
  DHT11 Humitidy and Temperature Sensor: DHT11 Humidity and Temperature Sensor
